# Fritzing sketch Musicarduino (saved by Fritzing 0.9.3b)
breadboards: 1

parts:
  Arduino_Uno = Arduino Uno (Rev3)
  R1 = Resistor [tolerance=±5% resistance=5.6k package=THT]
  D1 = Rectifier Diode [part_number=1S3 package="300 mil [THT]"]
  L1 = Solenoid [part_number="Sparkfun 5V solenoid"]
  Q1 = NPN-Transistor [part_number=2SC2458-Y package="TO92 [THT]"]
  R2 = Resistor [tolerance=±5% resistance=5.6k package=THT]
  D2 = Rectifier Diode [part_number=1S3 package="300 mil [THT]"]
  L2 = Solenoid [part_number="Sparkfun 5V solenoid"]
  Q2 = NPN-Transistor [part_number=2SC2458-Y package="TO92 [THT]"]
  Q3 = NPN-Transistor [part_number=2SC2458-Y package="TO92 [THT]"]
  L3 = Solenoid [part_number="Sparkfun 5V solenoid"]
  D3 = Rectifier Diode [part_number=1S3 package="300 mil [THT]"]
  D4 = Rectifier Diode [part_number=1S3 package="300 mil [THT]"]
  L4 = Solenoid [part_number="Sparkfun 5V solenoid"]
  Q4 = NPN-Transistor [part_number=2SC2458-Y package="TO92 [THT]"]
  R3 = Resistor [tolerance=±5% resistance=5.6k package=THT]
  R4 = Resistor [tolerance=±5% resistance=5.6k package=THT]
  D5 = Rectifier Diode [part_number=1S3 package="300 mil [THT]"]
  L5 = Solenoid [part_number="Sparkfun 5V solenoid"]
  Q5 = NPN-Transistor [part_number=2SC2458-Y package="TO92 [THT]"]
  R5 = Resistor [tolerance=±5% resistance=5.6k package=THT]
  IC1 = DIP - 24 pins [chip_label=PCA9547D part_number=I2CMUL package="DIP (Dual Inline) [THT]"]
  IC2 = IC, DIP package, 8 pins [chip_label=24FC1025-I/P part_number=EEPROM]
  S1 = Pushbutton [package="[THT]"]
  カラーセンサ1 = SHT1x-Breakout [part_number=S11059-02DT]  # not connected
  カラーセンサ2 = SHT1x-Breakout [part_number=S11059-02DT]
  LCD1 = LCD screen  # not connected
  R6 = Resistor [tolerance=±5% resistance=1.5k package=THT]
  R7 = Resistor [tolerance=±5% resistance=1.5k package=THT]
  R8 = Resistor [tolerance=±5% resistance=1.5k package=THT]
  R9 = Resistor [tolerance=±5% resistance=1.5k package=THT]
  R10 = Resistor [tolerance=±5% resistance=1.5k package=THT]
  C2 = Ceramic Capacitor [capacitance=0.1µF package="100 mil [THT, multilayer]"]
  R11 = Resistor [tolerance=±5% resistance=1.5k package=THT]
  R12 = Resistor [tolerance=±5% resistance=1.5k package=THT]

nets:
  N1: Arduino_Uno.A4/SDA, IC1.pin23, R7.Pin_1
  N2: Arduino_Uno.A5/SCL, IC1.pin22, R6.Pin_1
  N3: Arduino_Uno.D8, R1.Pin_0
  N4: Arduino_Uno.D9_PWM, R2.Pin_0
  N5: Arduino_Uno.D10_PWM/SS, R3.Pin_0
  N6: Arduino_Uno.D11_PWM/MOSI, R4.Pin_0
  N7: Arduino_Uno.D12/MISO, R5.Pin_0
  GND: Arduino_Uno.GND, Q4.E, IC1.A0, IC1.A1, IC1.pin12, IC2.pin1, IC2.pin2, IC2.pin4, IC2.pin7, S1.Pin_1, S1.Pin_2, C2.0
  N8: Arduino_Uno.D2, S1.Pin_3, S1.Pin_4
  N9: Arduino_Uno.3V3, IC2.pin8, R8.Pin_0, R9.Pin_0, R10.Pin_0, C2.1, R11.Pin_0, R12.Pin_0
  N10: Arduino_Uno.5V, D1.cathode, L1.pin1, Q1.E, D2.cathode, L2.pin1, Q2.E, Q3.E, L3.pin1, D3.cathode, D4.cathode, L4.pin1, D5.cathode, L5.pin1, Q5.E, IC1.RESET, IC1.pin24, R6.Pin_0, R7.Pin_0
  N11: R1.Pin_1, Q1.B
  N12: D1.anode, L1.pin2, Q1.C
  N13: R2.Pin_1, Q2.B
  N14: D2.anode, L2.pin2, Q2.C
  N15: Q3.B, R3.Pin_1
  N16: Q3.C, L3.pin2, D3.anode
  N17: D4.anode, L4.pin2, Q4.C
  N18: Q4.B, R4.Pin_1
  N19: D5.anode, L5.pin2, Q5.C
  N20: Q5.B, R5.Pin_1
  N21: IC1.pin4, IC2.pin5, R9.Pin_1
  N22: IC1.pin5, IC2.pin6, R8.Pin_1
  N23: IC1.pin6, カラーセンサ2.SCK, R12.Pin_1
  N24: IC1.pin7, カラーセンサ2.DATA, R11.Pin_1
  N25: IC2.pin3, R10.Pin_1

custom parts:
  DIP - 24 pins: A DIP stand-in part for whatever IC you want. With 24 pins on a 300mil dual inline package (DIP) footprint.
